// Logisim project test.circ as structural Verilog: 1 circuit, main circuit main
module main (
  input  in_1
);

  wire clock_1_out, undriven, undriven_2;
  wire [1:0] counter_1_q;
  wire [3:0] bit_extender_1_out, counter_2_q, multiplexer_1_out, multiplexer_2_out, multiplexer_3_out,
       ram_1_data, RS_q, undriven_3;

  Clock clock_1 (.out(clock_1_out));
  Counter #(.width(2), .max('h2)) counter_1 (
    .load(1'b0), .count(1'b1), .Q(counter_1_q), .clk(clock_1_out), .clr(in_1));  // open: D, carry
  Counter #(.width(4), .max('hf), .trigger("falling")) counter_2 (
    .load(1'b0), .count(1'b1), .Q(counter_2_q), .clk(clock_1_out), .clr(in_1));  // open: D, carry
  Decoder #(.select(2)) decoder_1 (.sel(counter_1_q), .en(1'b1));  // open: out0, out1, out2, out3
  RAM #(.addrWidth(4), .dataWidth(4)) ram_1 (.addr(counter_2_q), .data(ram_1_data));  // open: sel, clk, ld, clr
  Register #(.width(4)) RS (.D(ram_1_data), .en(undriven), .Q(RS_q), .clk(clock_1_out), .clr(in_1));
  Multiplexer #(.width(4)) multiplexer_1 (
    .in0(undriven_3), .in1(ram_1_data), .out(multiplexer_1_out), .en(1'b1));  // open: sel
  Register #(.width(4)) IR (.D(ram_1_data), .en(undriven_2), .clk(clock_1_out), .clr(in_1));  // open: Q
  assign bit_extender_1_out = {{3{1'b0}}, 1'b1};  // Bit_Extender bit_extender_1
  Multiplexer #(.width(4)) multiplexer_2 (
    .in0(RS_q), .in1(bit_extender_1_out), .out(multiplexer_2_out), .en(1'b1));  // open: sel
  Register #(.width(4), .trigger("falling")) register_1 (
    .D(multiplexer_1_out), .en(multiplexer_2_out[0]), .clk(clock_1_out), .clr(in_1));  // open: Q
  Register #(.width(4), .trigger("falling")) register_2 (
    .D(multiplexer_1_out), .en(multiplexer_2_out[1]), .clk(clock_1_out), .clr(in_1));  // open: Q
  Register #(.width(4), .trigger("falling")) register_3 (
    .D(multiplexer_1_out), .en(multiplexer_2_out[2]), .clk(clock_1_out), .clr(in_1));  // open: Q
  Register #(.width(4), .trigger("falling")) register_4 (
    .D(multiplexer_1_out), .en(multiplexer_2_out[3]), .clk(clock_1_out), .clr(in_1));  // open: Q
  Multiplexer #(.select(2), .width(4)) multiplexer_3 (.out(multiplexer_3_out));  // open: in0, in1, in2, in3, sel, en
  // ALU alu_1: pin names not known
endmodule
