// Logisim project test2.circ as structural Verilog: 1 circuit, main circuit main
module main (
  input  in_1
);

  wire and_1_out, clock_1_out, counter_1_carry, decoder_1_out2, decoder_1_out3, not_1_out, or_1_out, or_2_out;
  wire [1:0] counter_2_q;
  wire [3:0] counter_1_q, multiplexer_1_out, ram_1_data, register_1_q;

  or or_1 (or_1_out, decoder_1_out3, decoder_1_out2);
  not not_1 (not_1_out, or_1_out);
  and and_1 (and_1_out, not_1_out, clock_1_out);
  Clock clock_1 (.out(clock_1_out));
  Counter #(.width(4), .max('hf), .trigger("falling")) counter_1 (
    .load(1'b0), .count(1'b1), .Q(counter_1_q), .carry(counter_1_carry), .clk(and_1_out), .clr(in_1));  // open: D
  Multiplexer #(.width(4)) multiplexer_1 (
    .in0(counter_1_q), .in1(register_1_q), .out(multiplexer_1_out), .sel(decoder_1_out3), .en(1'b1));
  Decoder #(.select(2)) decoder_1 (
    .out2(decoder_1_out2), .out3(decoder_1_out3), .sel(counter_2_q), .en(1'b1));  // open: out0, out1
  Counter #(.width(2), .max('h3)) counter_2 (
    .load(1'b0), .count(1'b1), .Q(counter_2_q), .clk(clock_1_out), .clr(or_2_out));  // open: D, carry
  or or_2 (or_2_out, counter_1_carry, in_1);
  Register #(.width(4)) register_1 (
    .D(ram_1_data), .en(decoder_1_out2), .Q(register_1_q), .clk(clock_1_out), .clr(in_1));
  RAM #(.addrWidth(4), .dataWidth(4)) ram_1 (.addr(multiplexer_1_out), .data(ram_1_data));  // open: sel, clk, ld, clr
  Register #(.width(4), .trigger("falling")) register_2 (
    .D(ram_1_data), .en(decoder_1_out3), .clk(clock_1_out), .clr(in_1));  // open: Q
endmodule
